# Fritzing sketch Projet Station Sketch (saved by Fritzing 0.9.4)
circuit board: 6.05993cm x 5.34714cm
breadboards: 1

parts:
  Erreur = LED - 5mm [color="Red (633nm)" package="5 mm [THT]"]
  Enregistre = LED - 5mm [color="Green (555nm)" package="5 mm [THT]"]
  lit = LED - 5mm [color="Yellow (595nm)" package="5 mm [THT]"]
  R2 = Resistor [tolerance=±5% resistance=220 package=THT]
  R3 = Resistor [tolerance=±5% resistance=220 package=THT]
  R4 = Resistor [tolerance=±5% resistance=220 package=THT]
  v0_6_1_Station_C°_et_Hygro = Arduino Uno (Rev3)
  R1 = Resistor [tolerance=±5% resistance=10k package=THT]
  DHT22 = DHT22 Humidity and Temperature Sensor

nets:
  N1: Erreur.cathode, v0_6_1_Station_C°_et_Hygro.D5_PWM
  N2: Erreur.anode, R2.Pin_0
  N3: Enregistre.cathode, v0_6_1_Station_C°_et_Hygro.D6_PWM
  N4: Enregistre.anode, R3.Pin_0
  N5: lit.cathode, v0_6_1_Station_C°_et_Hygro.D7
  N6: lit.anode, R4.Pin_0
  GND: R2.Pin_1, R3.Pin_1, R4.Pin_1, v0_6_1_Station_C°_et_Hygro.GND, DHT22.GND
  N7: v0_6_1_Station_C°_et_Hygro.D2, R1.Pin_0, DHT22.DATA
  5V: v0_6_1_Station_C°_et_Hygro.5V, R1.Pin_1, DHT22.VDD
